# Fritzing sketch rpi (saved by Fritzing 0.9.10b)
breadboards: 1

parts:
  Raspberry_Pi_1 = Raspberry Pi 3 [part_number=RPI-3-V1.2]
  A1 = Raspberry Pi Pico H
  D1 = Zener Diode [part_number=1N4732A breakdown_voltage=3.6V package="300 mil [THT]"]
  R1 = Resistor [tolerance=±5% power=0.25 resistance=220 package=THT]
  R2 = Resistor [tolerance=±5% power=0.25 resistance=220 package=THT]
  LED1 = LED - 3mm [color="Red (633nm)" current=0.030 package="3 mm [THT]"]
  R3 = Resistor [tolerance=±5% power=0.25 resistance=220 package=THT]

nets:
  N1: Raspberry_Pi_1.3v3, D1.anode, R1.Pin_1, R2.Pin_1, R3.Pin_1
  N2: Raspberry_Pi_1.GPIO2, A1.GP20, R1.Pin_0
  N3: Raspberry_Pi_1.GPIO3, A1.GP21, R2.Pin_0
  N4: Raspberry_Pi_1.GPIO25, A1.SWCLK
  GND: Raspberry_Pi_1.GND, A1.GND
  N5: Raspberry_Pi_1.GPIO24, A1.SWDIO
  N6: Raspberry_Pi_1.GPIO18, LED1.cathode
  N7: A1.VSYS, D1.cathode
  N8: LED1.anode, R3.Pin_0

custom parts:
  Raspberry Pi Pico H: Raspberry Pi Pico H. Based around the RP2040 microcontroller the Pico H is a low cost microcontroller device bringing Raspberry Pi quality, cost, and easy of use to the microcontroller space.
