# Fritzing sketch ControllerModule (saved by Fritzing 0.9.10b)
breadboards: 1

parts:
  Part1 = Arduino Micro (Rev3)  # not connected
  M1 = Niren can bus module [package=THT]
  J1 = Power Jack [package=power_jack_pth]
  U1 = V_REG_LD1117VXX [package=78xxl]
  C1 = Capacitor [package=cap-pth-small-kit]
  C2 = Capacitor [package=cap-pth-small-kit]
  LED1 = LED - 3mm [color="Red (633nm)" current=0.030 package="3 mm [THT]"]  # not connected
  LED2 = LED - 3mm [color="Red (633nm)" current=0.030 package="3 mm [THT]"]  # not connected
  R1 = Resistor [tolerance=±5% resistance=220 package="2010 [SMD]"]  # not connected
  R2 = Resistor [tolerance=±5% resistance=220 package="2010 [SMD]"]  # not connected
  J2 = Screw terminal - 2 pins [package=THT]

nets:
  N1: M1.pin2, J1.GND, U1.OUT, C1.2, C2.2
  N2: M1.pin10, J2.pin1
  N3: M1.pin11, J2.pin2
  N4: J1.PWR, U1.GND, C2.1
  N5: U1.IN, C1.1

custom parts:
  Niren can bus module: Niren can bus module availabe on ebay and others. Pcb view assumes that you unsolder the 7 pin header and resolder it on the bottom of the module to connect to the pcb. The two jumpers and the can bus connector remain on the top of the board and don't appear in pcb view.
