# Fritzing sketch ControllerModuleRXTest (saved by Fritzing 0.9.10b)
breadboards: 1

parts:
  Part1 = Arduino Uno (Rev3) - ICSP
  LED1 = LED - 3mm [color="Red (633nm)" current=0.030 package="3 mm [THT]"]  # not connected
  R1 = Resistor [tolerance=±5% resistance=220 package="2010 [SMD]"]
  M1 = Niren can bus module [package=THT]

nets:
  N1: Part1.ICSP_MOSI, Part1.D11_PWM/MOSI, M1.pin5
  N2: Part1.D12/MISO, M1.pin4
  N3: Part1.D13/SCK, M1.pin6
  N4: Part1.GND, M1.pin2
  N5: Part1.D2, M1.pin7
  N6: Part1.D4, R1.Pin_0
  N7: Part1.D5_PWM, M1.pin3
  N8: Part1.5V, M1.pin1

custom parts:
  Niren can bus module: Niren can bus module availabe on ebay and others. Pcb view assumes that you unsolder the 7 pin header and resolder it on the bottom of the module to connect to the pcb. The two jumpers and the can bus connector remain on the top of the board and don't appear in pcb view.
