# Fritzing sketch arduino (saved by Fritzing 0.9.10b)
breadboards: 1

parts:
  A1 = Raspberry Pi Pico H
  Part1 = Arduino Micro (Rev3)  # not connected
  D1 = Diode [package=diode-1n4148]  # not connected
  R1 = Resistor [tolerance=±5% power=0.25 resistance=220 package=THT]
  R2 = Resistor [tolerance=±5% power=0.25 resistance=220 package=THT]

nets:
  N1: A1.GP20, R2.Pin_1
  N2: A1.GP21, R1.Pin_1
  N3: A1.3V3OUT, R1.Pin_0, R2.Pin_0

custom parts:
  Raspberry Pi Pico H: Raspberry Pi Pico H. Based around the RP2040 microcontroller the Pico H is a low cost microcontroller device bringing Raspberry Pi quality, cost, and easy of use to the microcontroller space.
